# Fritzing sketch self-driving_tank_bread (saved by Fritzing 0.9.3b)
breadboards: 1

parts:
  BAT4 = Battery Holders [package=lipo-1100mAh]
  BAT5 = Battery Holders [package=lipo-1100mAh]  # not connected
  パーツ4 = SRF05 Ultrasonic Rangefinder
  パーツ5 = SRF05 Ultrasonic Rangefinder
  パーツ6 = Arduino Nano (Rev3.0)
  パーツ7 = Motor Driver 1A Dual TB6612FNG  # not connected
  M3 = DC Motor
  M4 = DC Motor
  C3 = Ceramic Capacitor [capacitance=0.1nF package="100 mil [THT, multilayer]"]
  C4 = Ceramic Capacitor [capacitance=0.1nF package="100 mil [THT, multilayer]"]

nets:
  VCC: BAT4.+, パーツ4.VCC, パーツ5.VCC, パーツ6.VIN
  GND: BAT4.-, パーツ4.GND, パーツ5.GND, パーツ6.GND
  N1: パーツ4.Trig, パーツ6.D13/SCK
  N2: パーツ4.Echo, パーツ6.D12/MISO
  N3: パーツ5.Trig, パーツ6.D11/MOSI
  N4: パーツ5.Echo, パーツ6.D10
  N5: M3.pin_1, C4.0
  N6: M3.pin_2, C4.1
  N7: M4.pin_1, C3.0
  N8: M4.pin_2, C3.1

notes:
  右測距
  左測距
  右モータ
  左モータ
  動力用
  処理用
