# Fritzing sketch self-driving_tank_circuit_board (saved by Fritzing 0.9.3b)
perfboards: 1

parts:
  パーツ9 = Motor Driver 1A Dual TB6612FNG
  パーツ2 = Arduino Nano (Rev3.0)
  BAT7 = LIPO-1000mAh [package=lipo-1000]
  JP1 = Header 2 [package=molex-1x2_lock]
  JP2 = Header 2 [package=molex-1x2_lock]
  JP3 = Header 2 [package=molex-1x2_lock]
  JP4 = Header 2 [package=molex-1x2_lock]
  JP5 = Header 2 [package=molex-1x2_lock]
  JP6 = Header 2 [package=molex-1x2_lock]
  パーツ11 = SRF05 Ultrasonic Rangefinder [part_number=right]
  パーツ12 = SRF05 Ultrasonic Rangefinder [part_number=right]
  JP7 = Header 2 [package=molex-1x2_lock]
  JP8 = Header 2 [package=molex-1x2_lock]
  M7 = DC Motor
  M8 = DC Motor
  JP9 = Header 2 [package=molex-1x2_lock]
  JP10 = Header 2 [package=molex-1x2_lock]
  JP11 = Header 2 [package=molex-1x2_lock]
  JP12 = Header 2 [package=molex-1x2_lock]
  JP13 = Header 2 [package=molex-1x2_lock]
  JP14 = Header 2 [package=molex-1x2_lock]
  JP15 = Header 2 [package=molex-1x2_lock]
  BAT8 = LIPO-1000mAh [package=lipo-1000]
  JP16 = Header 2 [package=molex-1x2_lock]

nets:
  N1: パーツ9.B01, JP7.2
  N2: パーツ9.B02, JP7.1
  N3: パーツ9.A02, JP5.2
  N4: パーツ9.A01, JP5.1
  N5: パーツ9.GND, JP14.2
  N6: パーツ9.VCC, パーツ9.VM, JP14.1
  N7: パーツ9.PWMB, パーツ2.D9
  N8: パーツ2.D10, JP4.1
  N9: パーツ2.D11/MOSI, JP3.2
  N10: パーツ2.D12/MISO, JP2.1
  N11: パーツ2.VIN, JP1.1, JP3.1, JP13.1
  N12: パーツ2.GND, JP2.2, JP4.2, JP13.2
  N13: パーツ2.D13/SCK, JP1.2
  N14: BAT7.+, JP15.1
  N15: BAT7.-, JP15.2
  N16: JP6.1, M7.pin_1
  N17: JP6.2, M7.pin_2
  N18: パーツ11.VCC, JP12.1
  N19: パーツ11.Trig, JP12.2
  N20: パーツ11.Echo, JP11.1
  N21: パーツ11.GND, JP11.2
  N22: パーツ12.VCC, JP10.1
  N23: パーツ12.Trig, JP10.2
  N24: パーツ12.Echo, JP9.1
  N25: パーツ12.GND, JP9.2
  N26: JP8.1, M8.pin_1
  N27: JP8.2, M8.pin_2
  N28: BAT8.+, JP16.1
  N29: BAT8.-, JP16.2

notes:
  右測距
  右モータ
  左モータ
  左測距
  処理用
  動力用
